// Logisim project ex5.circ as structural Verilog: 5 circuits, main circuit rotr
module rotr (
  input  [15:0] A,
  input  [3:0] B,
  output [15:0] Out1
);

  wire not_1_out, not_2_out, not_3_out, not_4_out;
  wire [15:0] Result1, Result2, Result4, rot1_1_out_2, rot2_1_out_2, rot4_1_out_2, rot8_1_out_2;

  assign Result1 = B[0] ? rot1_1_out_2 : 16'bz;  // Controlled_Buffer controlled_buffer_1
  rot1 rot1_1 (.in_1(A), .out_2(rot1_1_out_2));
  not not_1 (not_1_out, B[0]);
  assign Result2 = B[1] ? rot2_1_out_2 : 16'bz;  // Controlled_Buffer controlled_buffer_2
  rot2 rot2_1 (.in_1(Result1), .out_2(rot2_1_out_2));
  assign Result4 = B[2] ? rot4_1_out_2 : 16'bz;  // Controlled_Buffer controlled_buffer_3
  rot4 rot4_1 (.in_1(Result2), .out_2(rot4_1_out_2));
  assign Out1 = B[3] ? rot8_1_out_2 : 16'bz;  // Controlled_Buffer controlled_buffer_4
  rot8 rot8_1 (.in_1(Result4), .out_2(rot8_1_out_2));
  assign Result1 = not_1_out ? A : 16'bz;  // Controlled_Buffer controlled_buffer_5
  not not_2 (not_2_out, B[1]);
  assign Result2 = not_2_out ? Result1 : 16'bz;  // Controlled_Buffer controlled_buffer_6
  not not_3 (not_3_out, B[2]);
  assign Result4 = not_3_out ? Result2 : 16'bz;  // Controlled_Buffer controlled_buffer_7
  not not_4 (not_4_out, B[3]);
  assign Out1 = not_4_out ? Result4 : 16'bz;  // Controlled_Buffer controlled_buffer_8

  // Other names for the same wires on the sheet: Allow1 = B[0]; Allow2 = B[1]; Allow4 = B[2]; Allow8 = B[3];
  //   entry[15:0] = A; Result8[15:0] = Out1

  // Notes on the sheet:
  //   PUT CIRCUITRY HERE
endmodule

module rot8 (
  input  [15:0] in_1,
  output [15:0] out_2
);

  wire [15:0] rot4_1_out_2;

  rot4 rot4_1 (.in_1(in_1), .out_2(rot4_1_out_2));
  rot4 rot4_2 (.in_1(rot4_1_out_2), .out_2(out_2));

  // Notes on the sheet:
  //   PUT CIRCUITRY HERE
endmodule

module rot4 (
  input  [15:0] in_1,
  output [15:0] out_2
);

  wire [15:0] rot2_1_out_2;

  rot2 rot2_1 (.in_1(in_1), .out_2(rot2_1_out_2));
  rot2 rot2_2 (.in_1(rot2_1_out_2), .out_2(out_2));

  // Notes on the sheet:
  //   PUT CIRCUITRY HERE
endmodule

module rot2 (
  input  [15:0] in_1,
  output [15:0] out_2
);

  wire [15:0] rot1_1_out_2;

  rot1 rot1_1 (.in_1(in_1), .out_2(rot1_1_out_2));
  rot1 rot1_2 (.in_1(rot1_1_out_2), .out_2(out_2));

  // Notes on the sheet:
  //   PUT CIRCUITRY HERE
endmodule

module rot1 (
  input  [15:0] in_1,
  output [15:0] out_2
);


  assign out_2 = {in_1[0], in_1[15:1]};

  // Notes on the sheet:
  //   PUT CIRCUITRY HERE
endmodule
