// Logisim project alu.circ as structural Verilog: 1 circuit, main circuit main
module main (
  input  [15:0] X,
  input  [15:0] Y,
  input  [2:0] Switch,
  output Equal,
  output [15:0] Result,
  output [15:0] Result_2_a9898de3
);

  wire result_sltBIN;
  wire [15:0] get4, get4_sll, result_add, result_and, result_mult, result_or, result_sll, result_slt,
       result_srl, result_xor, x_add, x_and, x_mult, x_or, x_sll, x_slt, x_srl, x_xor, y_add, y_and, y_mult,
       y_or, y_slt, y_xor;

  Demultiplexer #(.select(3), .width(16), .enable("false")) demultiplexer_1 (
    .out0(x_sll), .out1(x_srl), .out2(x_add), .out3(x_and), .out4(x_or), .out5(x_xor), .out6(x_slt),
    .out7(x_mult), .in(X), .sel(Switch));
  Demultiplexer #(.select(3), .width(16), .enable("false")) demultiplexer_2 (
    .out0(get4_sll), .out1(get4), .out2(y_add), .out3(y_and), .out4(y_or), .out5(y_xor), .out6(y_slt),
    .out7(y_mult), .in(Y), .sel(Switch));
  Comparator #(.width(16), .mode("unsigned")) comparator_1 (.a(X), .b(Y), .eq(Equal));  // open: gt, lt
  Adder #(.width(16)) adder_1 (.a(x_add), .b(y_add), .out(result_add));  // open: cin, cout
  assign result_and = x_and & y_and;  // AND_Gate and_1, 16 bits wide
  assign result_or = x_or | y_or;  // OR_Gate or_1, 16 bits wide
  assign result_xor = x_xor ^ y_xor;  // XOR_Gate xor_1, 16 bits wide
  Multiplier #(.width(16)) multiplier_1 (
    .a(x_mult), .b(y_mult), .out(result_mult), .cout(Result_2_a9898de3));  // open: cin
  Comparator #(.width(16)) comparator_2 (.a(x_slt), .b(y_slt), .lt(result_sltBIN));  // open: gt, eq
  assign result_slt = {{15{1'b0}}, result_sltBIN};  // Bit_Extender bit_extender_1
  Shifter #(.width(16)) shifter_1 (.in(x_sll), .\dist (get4_sll[3:0]), .out(result_sll));
  Shifter #(.width(16), .shift("lr")) shifter_2 (.in(x_srl), .\dist (get4[3:0]), .out(result_srl));
  Multiplexer #(.select(3), .width(16), .enable("false")) multiplexer_1 (
    .in0(result_sll), .in1(result_srl), .in2(result_add), .in3(result_and), .in4(result_or),
    .in5(result_xor), .in6(result_slt), .in7(result_mult), .out(Result), .sel(Switch));

  // Other names for the same wires on the sheet: result_2[15:0] = Result_2_a9898de3; S[2:0] = Switch;
  //   out4_sll[3:0] = get4_sll[3:0]; y_sll[15:0] = get4_sll; out4[3:0] = get4[3:0]; y_srl[15:0] = get4

  // Notes on the sheet:
  //   INPUTS to your circuit
  //   DON'T CHANGE THE LOCATIONS OF THE INPUTS AND OUTPUTS!
  //   OUTPUTS from your circuit
endmodule
