// Logisim project regfile-all.circ as structural Verilog: 1 circuit, main circuit main
module main (
  output [7:0] test_15c3af58,
  output [15:0] s0_Value_2fb9e1b0,
  output [15:0] s1_Value_65d4e6c2,
  output [15:0] s2_Value_4399d8a9,
  output [15:0] ra_Value_6de4aa9b,
  output [15:0] sp_Value_620c86e6,
  output [15:0] Read_Data_1_72bcd118,
  output [15:0] Read_Data_2_e13d58cc
);

  wire clock_1_out;
  wire [7:0] adder_1_out;
  wire [15:0] rom_2_data, WriteData;

  Register register_1 (.D(adder_1_out), .en(1'b1), .clk(clock_1_out), .Q(test_15c3af58));  // open: clr
  Adder adder_1 (.a(8'h1), .b(test_15c3af58), .out(adder_1_out));  // open: cin, cout
  ROM #(.dataWidth(16)) rom_1 (.addr(test_15c3af58), .data(WriteData));
  Clock clock_1 (.out(clock_1_out));
  ROM #(.dataWidth(16)) rom_2 (.addr(test_15c3af58), .data(rom_2_data));
  // regfile_main main_1: pin names not known; wires that end beside it: rom_2_data[2:0], rom_2_data[5:3], rom_2_data[8:6], s0_Value_2fb9e1b0, WriteData, s1_Value_65d4e6c2, rom_2_data[9], s2_Value_4399d8a9, clock_1_out, ra_Value_6de4aa9b, sp_Value_620c86e6, Read_Data_1_72bcd118, Read_Data_2_e13d58cc

  // Notes on the sheet:
  //   contents of rom_1 (hex, n*v repeats v):
  //   dead bad f00d 5678 1234 adf3 3216 341 6543 bc 0 31 3124 0 a78b 1982
  //   There should be no blue/red wires here, and the result shouldn't be x's.
  //   YOUR REGFILE SHOULD FIT IN HERE!
  //   contents of rom_2 (hex, n*v repeats v):
  //   20a 353 3a8 75 81 d5 312 3e6 27c 28a 297 3d7 3ff 17 17b 18c
endmodule
