// Logisim project cpu.circ as structural Verilog: 1 circuit, main circuit main
module main (
  input  [15:0] INSTRUCTION,
  input  CLOCK,
  output [15:0] FETCH_ADDRESS,
  output [15:0] L_s0_Value_7c9fba82,
  output [15:0] L_s1_Value_2cb75696,
  output [15:0] L_s2_Value_be7b1681,
  output [15:0] L_ra_Value_55886cf9,
  output [15:0] L_sp_Value_a0856b3d,
  output [15:0] L_HI_Value_3bde5b98,
  output [15:0] L_LO_Value_b62659ce
);

  Register #(.width(16)) L_PC_bd1e00e6 ();  // open: D, en, Q, clk, clr
  Register #(.width(16)) L_LO_ba622f5d ();  // open: D, en, Q, clk, clr
  Register #(.width(16)) L_HI_1d3f3066 ();  // open: D, en, Q, clk, clr
  // alu_main main_1: pin names not known
  // regfile_main main_2: pin names not known
  // mem_main MEM: pin names not known

  // Other names for the same wires on the sheet: clk = CLOCK; fetch_addr[15:0] = FETCH_ADDRESS

  // Notes on the sheet:
  //   Output
  //   These are outputs/inputs from run.circ
  //   Inputs
  //   These are DEBUG/TEST outputs from your circuit.
endmodule
