// Logisim project regfile.circ as structural Verilog: 1 circuit, main circuit main
module main (
  input  [2:0] Read_Register_1_eca808b4,
  input  [2:0] Read_Register_2_4b336a3e,
  input  [2:0] Write_Register_1c78e1ef,
  input  [15:0] Write_Data_00073c80,
  input  Write_Enable_5f560963,
  input  Clock,
  output [15:0] L_s0_Value_3e1de553,
  output [15:0] L_s1_Value_f16d02bf,
  output [15:0] L_s2_Value_6a9ed51f,
  output [15:0] L_ra_Value_b804995d,
  output [15:0] L_sp_Value_269f0ffd,
  output [15:0] Read_Data_1_c47ea0d8,
  output [15:0] Read_Data_2_34b29906,
  output [15:0] out_14,
  output [15:0] out_15,
  output [15:0] out_16,
  output [15:0] out_17,
  output [15:0] out_18,
  output [15:0] out_19,
  output [15:0] out_20,
  output [15:0] out_21
);

  wire demultiplexer_2_out1, demultiplexer_2_out2, demultiplexer_2_out3, demultiplexer_2_out4,
       demultiplexer_2_out5, demultiplexer_2_out6, demultiplexer_2_out7;
  wire [15:0] demultiplexer_1_out0, demultiplexer_1_out1, demultiplexer_1_out2, demultiplexer_1_out3,
       demultiplexer_1_out4, demultiplexer_1_out5, demultiplexer_1_out6, demultiplexer_1_out7;

  Demultiplexer #(.select(3), .width(16), .enable("false")) demultiplexer_1 (
    .out0(demultiplexer_1_out0), .out1(demultiplexer_1_out1), .out2(demultiplexer_1_out2),
    .out3(demultiplexer_1_out3), .out4(demultiplexer_1_out4), .out5(demultiplexer_1_out5),
    .out6(demultiplexer_1_out6), .out7(demultiplexer_1_out7), .in(Write_Data_00073c80),
    .sel(Write_Register_1c78e1ef));
  Demultiplexer #(.select(3), .enable("false")) demultiplexer_2 (
    .out1(demultiplexer_2_out1), .out2(demultiplexer_2_out2), .out3(demultiplexer_2_out3),
    .out4(demultiplexer_2_out4), .out5(demultiplexer_2_out5), .out6(demultiplexer_2_out6),
    .out7(demultiplexer_2_out7), .in(Write_Enable_5f560963), .sel(Write_Register_1c78e1ef));  // open: out0
  Register #(.width(16)) R0 (.D(demultiplexer_1_out0), .en(1'b0), .clk(Clock), .Q(out_14));  // open: clr
  Register #(.width(16)) R1 (
    .D(demultiplexer_1_out1), .en(demultiplexer_2_out1), .clk(Clock), .Q(L_ra_Value_b804995d));  // open: clr
  Register #(.width(16)) R2 (
    .D(demultiplexer_1_out2), .en(demultiplexer_2_out2), .clk(Clock), .Q(L_s0_Value_3e1de553));  // open: clr
  Register #(.width(16)) R3 (
    .D(demultiplexer_1_out3), .en(demultiplexer_2_out3), .clk(Clock), .Q(L_s1_Value_f16d02bf));  // open: clr
  Register #(.width(16)) R4 (
    .D(demultiplexer_1_out4), .en(demultiplexer_2_out4), .clk(Clock), .Q(L_s2_Value_6a9ed51f));  // open: clr
  Register #(.width(16)) R5 (
    .D(demultiplexer_1_out5), .en(demultiplexer_2_out5), .clk(Clock), .Q(out_19));  // open: clr
  Register #(.width(16)) R6 (
    .D(demultiplexer_1_out6), .en(demultiplexer_2_out6), .clk(Clock), .Q(out_20));  // open: clr
  Register #(.width(16)) R7 (
    .D(demultiplexer_1_out7), .en(demultiplexer_2_out7), .clk(Clock), .Q(L_sp_Value_269f0ffd));  // open: clr
  Multiplexer #(.select(3), .width(16), .enable("false")) multiplexer_1 (
    .in0(out_14), .in1(L_ra_Value_b804995d), .in2(L_s0_Value_3e1de553), .in3(L_s1_Value_f16d02bf),
    .in4(L_s2_Value_6a9ed51f), .in5(out_19), .in6(out_20), .in7(L_sp_Value_269f0ffd),
    .out(Read_Data_1_c47ea0d8), .sel(Read_Register_1_eca808b4));
  Multiplexer #(.select(3), .width(16), .enable("false")) multiplexer_2 (
    .in0(out_14), .in1(L_ra_Value_b804995d), .in2(L_s0_Value_3e1de553), .in3(L_s1_Value_f16d02bf),
    .in4(L_s2_Value_6a9ed51f), .in5(out_19), .in6(out_20), .in7(L_sp_Value_269f0ffd),
    .out(Read_Data_2_34b29906), .sel(Read_Register_2_4b336a3e));

  assign out_15 = L_ra_Value_b804995d;
  assign out_16 = L_s0_Value_3e1de553;
  assign out_17 = L_s1_Value_f16d02bf;
  assign out_18 = L_s2_Value_6a9ed51f;
  assign out_21 = L_sp_Value_269f0ffd;

  // Other names for the same wires on the sheet: clk = Clock; R0[15:0] = out_14; R1[15:0] = L_ra_Value_b804995d;
  //   R2[15:0] = L_s0_Value_3e1de553; R3[15:0] = L_s1_Value_f16d02bf; R4[15:0] = L_s2_Value_6a9ed51f;
  //   R5[15:0] = out_19; R6[15:0] = out_20; R7[15:0] = L_sp_Value_269f0ffd; read_data1[15:0] = Read_Data_1_c47ea0d8;
  //   read_data2[15:0] = Read_Data_2_34b29906; read_reg1[2:0] = Read_Register_1_eca808b4;
  //   read_reg2[2:0] = Read_Register_2_4b336a3e; write_data[15:0] = Write_Data_00073c80;
  //   write_en = Write_Enable_5f560963; write_reg[2:0] = Write_Register_1c78e1ef

  // Notes on the sheet:
  //   INPUTS to your circuit
  //   DON'T CHANGE THE LOCATIONS OF THE INPUTS AND OUTPUTS!
  //   These are DEBUG/TEST outputs from your circuit.
  //   OUTPUTS from your circuit
endmodule
