// Logisim project CPU - Projeto de PCL-backup.circ as structural Verilog: 4 circuits, main circuit main
module main (
  input  [4:0] in_1,
  output [7:0] out_2,
  output [7:0] out_3,
  output [7:0] out_4,
  output [7:0] out_5,
  output [7:0] out_6,
  output [7:0] out_7
);

  wire clock, clock_1_out, HLT, not_1_out, or_1_out, R___RAM_P, RA___R_P, RAM___R_P, Rx_Ry, Ry___Rx_P;
  wire [1:0] controlled_buffer_3_out, end_R, end_RAM;
  wire [3:0] INST;
  wire [4:0] Contador_de_Programa_q;
  wire [7:0] R0, R1, R2, R3, Ry;

  Clock clock_1 (.out(clock_1_out));
  assign clock = not_1_out ? clock_1_out : 1'bz;  // Controlled_Buffer controlled_buffer_1
  not not_1 (not_1_out, HLT);
  Counter #(.width(5), .max('h1f)) Contador_de_Programa (
    .D(in_1), .Q(Contador_de_Programa_q), .clk(clock));  // open: load, count, carry, clr
  Register \Registrador_Instrução  (.D(out_2), .Q({INST, end_R, end_RAM}), .clk(clock));  // open: en, clr
  Decodificador decodificador_1 (
    .Entrada_4_bits(INST), .permite_soma(Rx_Ry), .Encerramento(HLT), .copia_R_em_R(Ry___Rx_P),
    .Copia_Ra_em_R(RA___R_P), .poe_end_dados_em_R(RAM___R_P), .poe_R_em_end_dados(R___RAM_P));
  Register RA (.D(out_6), .en(Rx_Ry), .Q(out_5), .clk(clock));  // open: clr
  Registradores registradores_1 (
    .dados(out_4), .end_Rx(end_R), .clock(clock), .out_6(R0), .out_7(R1), .out_8(R2), .out_9(R3),
    .R___RAM(R___RAM_P), .Byte_pra_RAM(out_7));
  ROM #(.addrWidth(5)) rom_1 (.addr(Contador_de_Programa_q), .data(out_2));  // open: sel
  assign out_4 = RA___R_P ? out_5 : 8'bz;  // Controlled_Buffer controlled_buffer_2
  assign controlled_buffer_3_out = or_1_out ? end_RAM : 2'bz;  // Controlled_Buffer controlled_buffer_3
  or or_1 (or_1_out, R___RAM_P, RAM___R_P);
  assign out_4 = Ry___Rx_P ? Ry : 8'bz;  // Controlled_Buffer controlled_buffer_4
  assign out_4 = RAM___R_P ? out_3 : 8'bz;  // Controlled_Buffer controlled_buffer_5
  Multiplexer #(.select(2), .width(8)) multiplexer_1 (
    .in0(R0), .in1(R1), .in2(R2), .in3(R3), .out(Ry), .sel(end_RAM), .en(Ry___Rx_P));
  ALU alu_1 (.R0(R0), .R1(R1), .Rx(end_R), .R2(R2), .R3(R3), .Ry(end_RAM), .out_8(out_6), .in_6(Rx_Ry));
  RAM #(.addrWidth(2), .bus("separate")) ram_1 (
    .addr(controlled_buffer_3_out), .din(out_7), .data(out_3), .str(R___RAM_P), .clk(clock), .ld(RAM___R_P));  // open: sel, clr

  // Other names for the same wires on the sheet: byte_pra_RAM[7:0] = out_7; byte_RAM[7:0] = out_3;
  //   out_ROM[7:0] = out_2; R_IN[7:0] = out_4; RA[7:0] = out_6; RA_____Rx[7:0] = out_5

  // Notes on the sheet:
  //   MEMORIA ROM
  //   contents of rom_1 (hex, n*v repeats v):
  //   d0 d5 da df 91 c4 9b c8 96 cc ec 80
  //   MEMORIA RAM
endmodule

// Unidade de \n controle
module Decodificador (
  input  [3:0] Entrada_4_bits,
  output permite_soma,
  output Encerramento,
  output copia_R_em_R,
  output Copia_Ra_em_R,
  output poe_end_dados_em_R,
  output poe_R_em_end_dados
);

  Comparator #(.width(4)) comparator_1 (.a(Entrada_4_bits), .b(4'b1001), .eq(permite_soma));  // open: gt, lt
  Comparator #(.width(4)) comparator_2 (.a(Entrada_4_bits), .b(4'b1000), .eq(Encerramento));  // open: gt, lt
  Comparator #(.width(4)) comparator_3 (.a(Entrada_4_bits), .b(4'b1011), .eq(copia_R_em_R));  // open: gt, lt
  Comparator #(.width(4)) comparator_4 (.a(Entrada_4_bits), .b(4'b1100), .eq(Copia_Ra_em_R));  // open: gt, lt
  Comparator #(.width(4)) comparator_5 (.a(Entrada_4_bits), .b(4'b1101), .eq(poe_end_dados_em_R));  // open: gt, lt
  Comparator #(.width(4)) comparator_6 (.a(Entrada_4_bits), .b(4'b1110), .eq(poe_R_em_end_dados));  // open: gt, lt
endmodule

module Registradores (
  input  [7:0] dados,
  input  [1:0] end_Rx,
  input  clock,
  input  R___RAM,
  output [7:0] Byte_pra_RAM,
  output [7:0] out_6,
  output [7:0] out_7,
  output [7:0] out_8,
  output [7:0] out_9
);

  wire comparator_1_eq, comparator_2_eq, comparator_3_eq, comparator_4_eq;
  wire [7:0] controlled_buffer_1_out, controlled_buffer_2_out, controlled_buffer_3_out,
       controlled_buffer_4_out, controlled_buffer_5_out;

  Comparator #(.width(2)) comparator_1 (.a(end_Rx), .b(2'b00), .eq(comparator_1_eq));  // open: gt, lt
  Comparator #(.width(2)) comparator_2 (.a(end_Rx), .b(2'b01), .eq(comparator_2_eq));  // open: gt, lt
  Comparator #(.width(2)) comparator_3 (.a(end_Rx), .b(2'b10), .eq(comparator_3_eq));  // open: gt, lt
  Comparator #(.width(2)) comparator_4 (.a(end_Rx), .b(2'b11), .eq(comparator_4_eq));  // open: gt, lt
  assign controlled_buffer_1_out = comparator_2_eq ? dados : 8'bz;  // Controlled_Buffer controlled_buffer_1
  assign controlled_buffer_2_out = comparator_1_eq ? dados : 8'bz;  // Controlled_Buffer controlled_buffer_2
  Register R0_00 (.D(controlled_buffer_2_out), .Q(out_6), .clk(clock));  // open: en, clr
  Register R1_01 (.D(controlled_buffer_1_out), .Q(out_7), .clk(clock));  // open: en, clr
  Register R2_02 (.D(controlled_buffer_3_out), .Q(out_8), .clk(clock));  // open: en, clr
  assign controlled_buffer_3_out = comparator_3_eq ? dados : 8'bz;  // Controlled_Buffer controlled_buffer_3
  Register R3_03 (.D(controlled_buffer_4_out), .Q(out_9), .clk(clock));  // open: en, clr
  assign controlled_buffer_4_out = comparator_4_eq ? dados : 8'bz;  // Controlled_Buffer controlled_buffer_4
  assign controlled_buffer_5_out = comparator_4_eq ? out_9 : 8'bz;  // Controlled_Buffer controlled_buffer_5
  assign controlled_buffer_5_out = comparator_1_eq ? out_6 : 8'bz;  // Controlled_Buffer controlled_buffer_6
  assign controlled_buffer_5_out = comparator_2_eq ? out_7 : 8'bz;  // Controlled_Buffer controlled_buffer_7
  assign controlled_buffer_5_out = comparator_3_eq ? out_8 : 8'bz;  // Controlled_Buffer controlled_buffer_8
  assign Byte_pra_RAM = R___RAM ? controlled_buffer_5_out : 8'bz;  // Controlled_Buffer controlled_buffer_9
endmodule

module ALU (
  input  [7:0] R0,
  input  [1:0] Rx,
  input  [7:0] R1,
  input  [7:0] R2,
  input  [7:0] R3,
  input  in_6,
  input  [1:0] Ry,
  output [7:0] out_8
);

  wire [7:0] multiplexer_1_out, multiplexer_2_out;

  Multiplexer #(.select(2), .width(8)) multiplexer_1 (
    .in0(R0), .in1(R1), .in2(R2), .in3(R3), .out(multiplexer_1_out), .sel(Rx), .en(in_6));
  Multiplexer #(.select(2), .width(8)) multiplexer_2 (
    .in0(R0), .in1(R1), .in2(R2), .in3(R3), .out(multiplexer_2_out), .sel(Ry), .en(in_6));
  Adder adder_1 (.a(multiplexer_1_out), .b(multiplexer_2_out), .out(out_8));  // open: cin, cout
endmodule
